// Digital circuit ALU.dig as structural Verilog
module ALU (
  input  [2:0] ALUOp,
  input  [31:0] A,
  input  [31:0] B,
  output [31:0] R,
  output N,
  output Z,
  output C,
  output V,
  output [3:0] NZCV
);

  wire and_2_out, and_3_out, comparator_2_gt, comparator_2_lt, comparator_3_gt, comparator_3_lt,
       comparator_4_gt, comparator_4_lt;
  wire [31:0] ADD_s, and_1_out, barrelshifter_1_out, barrelshifter_2_out, RSB_s, SUB_s;
  wire [63:0] MUL_mul;

  Add #(.Bits(32)) ADD (.a(A), .b(B), .c_i(1'b0), .s(ADD_s));  // open: c_o
  Sub #(.Bits(32)) SUB (.a(A), .b(B), .c_i(1'b0), .s(SUB_s));  // open: c_o
  Mul #(.Bits(32)) MUL (.a(A), .b(B), .mul(MUL_mul));
  Sub #(.Bits(32)) RSB (.a(B), .b(A), .c_i(1'b0), .s(RSB_s));  // open: c_o
  BarrelShifter #(.Bits(32)) barrelshifter_1 (.in(A), .shift(B[5:0]), .out(barrelshifter_1_out));
  BarrelShifter #(.Bits(32), .direction("right")) barrelshifter_2 (.in(A), .shift(B[5:0]), .out(barrelshifter_2_out));
  assign and_1_out = A & B;  // And and_1, 32 bits wide
  Comparator #(.Bits(32)) comparator_1 (.a(A), .b(B), .lt(C));  // open: gt, eq
  Comparator #(.Bits(32)) comparator_2 (.a(A), .b(B), .gt(comparator_2_gt), .lt(comparator_2_lt));  // open: eq
  Comparator #(.Bits(32)) comparator_3 (.a(A), .b(B), .gt(comparator_3_gt), .lt(comparator_3_lt));  // open: eq
  Comparator #(.Bits(32)) comparator_4 (
    .a(ADD_s), .b({32{1'b0}}), .gt(comparator_4_gt), .lt(comparator_4_lt));  // open: eq
  Multiplexer #(.Selector_Bits(3), .Bits(32)) multiplexer_1 (
    .sel(ALUOp), .in_0(ADD_s), .in_1(SUB_s), .in_2(MUL_mul[31:0]), .in_3(B), .in_4(RSB_s), .in_5({32{1'b0}}),
    .in_6({32{1'b0}}), .in_7(and_1_out), .out(R));
  and and_2 (and_2_out, comparator_3_gt, comparator_4_lt, comparator_2_lt);
  and and_3 (and_3_out, comparator_4_gt, comparator_2_gt, comparator_3_lt);
  or or_1 (NZCV[3], and_2_out, and_3_out);
  Comparator #(.Signed("true"), .Bits(32)) comparator_5 (.a(R), .b({32{1'b0}}), .lt(N));  // open: gt, eq
  Comparator #(.Bits(32)) comparator_6 (.a(R), .b({32{1'b0}}), .eq(NZCV[1]));  // open: gt, lt

  assign {NZCV[2], NZCV[0]} = {C, N};
  assign V = NZCV[3];
  assign Z = NZCV[1];
endmodule
