// Digital circuit control_unit.dig as structural Verilog
module control_unit (
  input  [31:0] iw,
  input  [3:0] NCZV,
  input  CLK,
  output RFW,
  output [1:0] EXTop,
  output ALUsrcB,
  output [2:0] ALUop,
  output [1:0] PCsel,
  output [1:0] RR0sel,
  output [1:0] RR1sel,
  output RR2sel,
  output [1:0] WRsel,
  output WDsel,
  output MR,
  output MW,
  output SHen
);

  wire AL_eq, and_1_out, and_2_out, and_3_out, and_4_out, and_5_out, and_6_out, and_7_out, and_8_out,
       and_9_out, and_10_out, and_11_out, and_12_out, and_13_out, and_14_out, and_15_out, and_16_out, C,
       CC_eq, comparator_1_gt, comparator_1_lt, comparator_2_eq, comparator_3_gt, comparator_3_lt,
       comparator_4_eq, condex, CS_eq, decoder_1_cpsrw, EQ_eq, GE_eq, GT_eq, HI_eq, LE_eq, LS_eq, LT_eq,
       MI_eq, N, NE_eq, or_1_out, or_2_out, or_3_out, or_4_out, PL_eq, V, VC_eq, VS_eq, Z;
  wire [1:0] decoder_1_pcsel;

  Comparator comparator_1 (.a(N), .b(V), .gt(comparator_1_gt), .lt(comparator_1_lt));  // open: eq
  Comparator comparator_2 (.a(N), .b(V), .eq(comparator_2_eq));  // open: gt, lt
  Comparator comparator_3 (.a(N), .b(V), .gt(comparator_3_gt), .lt(comparator_3_lt));  // open: eq
  Comparator #(.Bits(4)) AL (.a(iw[31:28]), .b(4'b1110), .eq(AL_eq));  // open: gt, lt
  Comparator #(.Bits(4)) EQ (.a(iw[31:28]), .b(4'b0000), .eq(EQ_eq));  // open: gt, lt
  Comparator #(.Bits(4)) NE (.a(iw[31:28]), .b(4'b0001), .eq(NE_eq));  // open: gt, lt
  Comparator #(.Bits(4)) CS (.a(iw[31:28]), .b(4'b0010), .eq(CS_eq));  // open: gt, lt
  Comparator #(.Bits(4)) CC (.a(iw[31:28]), .b(4'b0011), .eq(CC_eq));  // open: gt, lt
  Comparator #(.Bits(4)) MI (.a(iw[31:28]), .b(4'b0100), .eq(MI_eq));  // open: gt, lt
  Comparator #(.Bits(4)) PL (.a(iw[31:28]), .b(4'b0101), .eq(PL_eq));  // open: gt, lt
  Comparator #(.Bits(4)) VS (.a(iw[31:28]), .b(4'b0110), .eq(VS_eq));  // open: gt, lt
  Comparator #(.Bits(4)) VC (.a(iw[31:28]), .b(4'b0111), .eq(VC_eq));  // open: gt, lt
  Comparator #(.Bits(4)) HI (.a(iw[31:28]), .b(4'b1000), .eq(HI_eq));  // open: gt, lt
  and and_1 (and_1_out, C, ~Z);  // And
  Comparator #(.Bits(4)) LS (.a(iw[31:28]), .b(4'b1001), .eq(LS_eq));  // open: gt, lt
  or or_1 (or_1_out, ~C, Z);  // Or
  Comparator #(.Bits(4)) GE (.a(iw[31:28]), .b(4'b1010), .eq(GE_eq));  // open: gt, lt
  Comparator comparator_4 (.a(N), .b(V), .eq(comparator_4_eq));  // open: gt, lt
  Comparator #(.Bits(4)) LT (.a(iw[31:28]), .b(4'b1011), .eq(LT_eq));  // open: gt, lt
  or or_2 (or_2_out, comparator_1_gt, comparator_1_lt);
  Comparator #(.Bits(4)) GT (.a(iw[31:28]), .b(4'b1100), .eq(GT_eq));  // open: gt, lt
  Comparator #(.Bits(4)) LE (.a(iw[31:28]), .b(4'b1101), .eq(LE_eq));  // open: gt, lt
  or or_3 (or_3_out, comparator_3_gt, comparator_3_lt);
  Register #(.Bits(4)) CPSR (.D(NCZV), .C(CLK), .en(decoder_1_cpsrw), .Q({V, C, Z, N}));
  and and_2 (and_2_out, comparator_2_eq, ~Z);  // And
  decoder decoder_1 (
    .IW(iw), .CPSRW(decoder_1_cpsrw), .SHen(SHen), .MW(MW), .MR(MR), .WDsel(WDsel), .WRsel(WRsel),
    .RR2sel(RR2sel), .RR1sel(RR1sel), .RR0sel(RR0sel), .PCsel(decoder_1_pcsel), .ALUop(ALUop),
    .ALUsrcB(ALUsrcB), .EXTop(EXTop), .RFW(RFW));
  and and_3 (and_3_out, EQ_eq, Z);
  and and_4 (and_4_out, NE_eq, ~Z);  // And
  and and_5 (and_5_out, CS_eq, C);
  and and_6 (and_6_out, CC_eq, ~C);  // And
  and and_7 (and_7_out, MI_eq, N);
  and and_8 (and_8_out, PL_eq, ~N);  // And
  and and_9 (and_9_out, VS_eq, V);
  and and_10 (and_10_out, VC_eq, ~V);  // And
  and and_11 (and_11_out, HI_eq, and_1_out);
  and and_12 (and_12_out, LS_eq, or_1_out);
  and and_13 (and_13_out, GE_eq, comparator_4_eq);
  and and_14 (and_14_out, LT_eq, or_2_out);
  and and_15 (and_15_out, GT_eq, and_2_out);
  or or_4 (or_4_out, or_3_out, Z);
  and and_16 (and_16_out, LE_eq, or_4_out);
  Multiplexer #(.Bits(2)) multiplexer_1 (.sel(condex), .in_0(2'b00), .in_1(decoder_1_pcsel), .out(PCsel));
  or or_5 (condex, AL_eq, and_3_out, and_4_out, and_5_out, and_6_out, and_7_out, and_8_out, and_9_out, and_10_out, and_11_out, and_12_out, and_13_out, and_14_out, and_15_out, and_16_out);
endmodule
