// Digital circuit decoder.dig as structural Verilog
module decoder (
  input  [31:0] IW,
  output [2:0] ALUop,
  output ALUsrcB,
  output [1:0] EXTop,
  output RFW,
  output WDsel,
  output [1:0] WRsel,
  output [1:0] RR1sel,
  output [1:0] RR0sel,
  output [1:0] PCsel,
  output RR2sel,
  output MR,
  output MW,
  output SHen,
  output CPSRW
);

  wire add_i_eq, add_r_eq, and_1_out, and_i_eq, and_r_eq, b_eq, bl_eq, bx_eq, cmp_i_eq, cmp_r_eq, ldr_i_eq,
       ldr_r_eq, mov_i_eq, mov_r_eq, mul_cond1_eq, mul_cond2_eq, rsb_i_eq, rsb_r_eq, str_i_eq, str_r_eq,
       sub_i_eq, sub_r_eq;
  wire [4:0] priorityencoder_1_num;

  // Probe on IW[27:20]
  // Probe on IW[27:24]
  // Probe on IW[27:4]
  // Probe on IW[27:22]
  // Probe on IW[7:4]
  // Probe on IW[6:5]
  Comparator #(.Bits(8)) add_r (.a(IW[27:20]), .b(8'h8), .eq(add_r_eq));  // open: gt, lt
  Comparator #(.Bits(8)) add_i (.a(IW[27:20]), .b(8'h28), .eq(add_i_eq));  // open: gt, lt
  Comparator #(.Bits(8)) mov_r (.a(IW[27:20]), .b(8'h1a), .eq(mov_r_eq));  // open: gt, lt
  Comparator #(.Bits(8)) mov_i (.a(IW[27:20]), .b(8'h3a), .eq(mov_i_eq));  // open: gt, lt
  Comparator #(.Bits(8)) sub_r (.a(IW[27:20]), .b(8'h4), .eq(sub_r_eq));  // open: gt, lt
  Comparator #(.Bits(8)) sub_i (.a(IW[27:20]), .b(8'h24), .eq(sub_i_eq));  // open: gt, lt
  Comparator #(.Bits(8)) rsb_r (.a(IW[27:20]), .b(8'h6), .eq(rsb_r_eq));  // open: gt, lt
  Comparator #(.Bits(8)) rsb_i (.a(IW[27:20]), .b(8'h26), .eq(rsb_i_eq));  // open: gt, lt
  Comparator #(.Bits(8)) and_r (.a(IW[27:20]), .b({8{1'b0}}), .eq(and_r_eq));  // open: gt, lt
  Comparator #(.Bits(8)) and_i (.a(IW[27:20]), .b(8'h20), .eq(and_i_eq));  // open: gt, lt
  Comparator #(.Bits(8)) cmp_r (.a(IW[27:20]), .b(8'h15), .eq(cmp_r_eq));  // open: gt, lt
  Comparator #(.Bits(8)) cmp_i (.a(IW[27:20]), .b(8'h35), .eq(cmp_i_eq));  // open: gt, lt
  Comparator #(.Bits(8)) ldr_r (.a(IW[27:20]), .b(8'h79), .eq(ldr_r_eq));  // open: gt, lt
  Comparator #(.Bits(8)) ldr_i (.a(IW[27:20]), .b(8'h59), .eq(ldr_i_eq));  // open: gt, lt
  Comparator #(.Bits(8)) str_r (.a(IW[27:20]), .b(8'h78), .eq(str_r_eq));  // open: gt, lt
  Comparator #(.Bits(8)) str_i (.a(IW[27:20]), .b(8'h58), .eq(str_i_eq));  // open: gt, lt
  Comparator #(.Bits(6)) mul_cond1 (.a(IW[27:22]), .b({6{1'b0}}), .eq(mul_cond1_eq));  // open: gt, lt
  Comparator #(.Bits(4)) mul_cond2 (.a(IW[7:4]), .b(4'b1001), .eq(mul_cond2_eq));  // open: gt, lt
  Comparator #(.Bits(4)) b (.a(IW[27:24]), .b(4'b1010), .eq(b_eq));  // open: gt, lt
  Comparator #(.Bits(4)) bl (.a(IW[27:24]), .b(4'b1011), .eq(bl_eq));  // open: gt, lt
  Comparator #(.Bits(24)) bx (.a(IW[27:4]), .b(24'h12fff1), .eq(bx_eq));  // open: gt, lt
  and and_1 (and_1_out, mul_cond1_eq, mul_cond2_eq);
  PriorityEncoder #(.Selector_Bits(5)) priorityencoder_1 (
    .in0(add_r_eq), .in1(add_i_eq), .in2(mov_r_eq), .in3(mov_i_eq), .in4(sub_r_eq), .in5(sub_i_eq),
    .in6(rsb_r_eq), .in7(rsb_i_eq), .in8(and_r_eq), .in9(and_i_eq), .in10(cmp_r_eq), .in11(cmp_i_eq),
    .in12(ldr_r_eq), .in13(ldr_i_eq), .in14(str_r_eq), .in15(str_i_eq), .in16(and_1_out), .in17(b_eq),
    .in18(bl_eq), .in19(bx_eq), .in20(1'b0), .in21(1'b0), .in22(1'b0), .in23(1'b0), .in24(1'b0), .in25(1'b0),
    .in26(1'b0), .in27(1'b0), .in28(1'b0), .in29(1'b0), .in30(1'b0), .in31(1'b0), .num(priorityencoder_1_num));  // open: any
  ROM #(.AddrBits(5), .Bits(21)) rom_1 (
    .A(priorityencoder_1_num), .sel(1'b1),
    .D({RFW, EXTop, ALUsrcB, ALUop, PCsel, RR0sel, RR1sel, RR2sel, WRsel, WDsel, MR, MW, SHen, CPSRW}));
  // Probe on {RFW, EXTop, ALUsrcB, ALUop, PCsel, RR0sel, RR1sel, RR2sel, WRsel, WDsel, MR, MW, SHen, CPSRW}
  // Probe on CPSRW
  // Probe on SHen
  // Probe on MW
  // Probe on MR
  // Probe on WDsel
  // Probe on WRsel
  // Probe on RR2sel
  // Probe on RR1sel
  // Probe on RR0sel
  // Probe on PCsel
  // Probe on ALUop
  // Probe on ALUsrcB
  // Probe on EXTop
  // Probe on RFW

  // Other names for the same wires on the sheet: bits7_4[3:0] = IW[7:4]; bits27_4[23:0] = IW[27:4];
  //   bits6_5[1:0] = IW[6:5]; bits27_20[7:0] = IW[27:20]; bits27_22[5:0] = IW[27:22]; bits27_24[3:0] = IW[27:24]

  // Notes on the sheet:
  //   contents of rom_1 (hex, n*v repeats v):
  //   100000,120000,10c002,12c002,104000,124000,110000,130000,11c000
  //   ,13c000,4001,24001,14000a,160088,40106,60184,108a40,a1400,1a1430
  //   ,2000,114000,134002,118000,138002
endmodule
