// Digital circuit decoder_rev2.dig as structural Verilog
module decoder_rev2 (
  input  [31:0] IW,
  output [2:0] ALUop,
  output ALUsrcB,
  output [1:0] EXTop,
  output RFW
);

  wire add_r_eq, mov_i_eq, priorityencoder_1_num;
  wire [8:0] multiplexer_1_out;

  // Probe on IW[27:20]
  Comparator #(.Bits(8)) add_r (.a(IW[27:20]), .b(8'h8), .eq(add_r_eq));  // open: gt, lt
  Comparator #(.Bits(8)) mov_i (.a(IW[27:20]), .b(8'h3a), .eq(mov_i_eq));  // open: gt, lt
  PriorityEncoder priorityencoder_1 (.in0(add_r_eq), .in1(mov_i_eq), .num(priorityencoder_1_num));  // open: any
  Multiplexer #(.Bits(16)) multiplexer_1 (
    .sel(priorityencoder_1_num), .in_0(16'h8000), .in_1(16'h9600),
    .out({RFW, EXTop, ALUsrcB, ALUop, multiplexer_1_out}));
  // Probe on {RFW, EXTop, ALUsrcB, ALUop, multiplexer_1_out}
  // Probe on ALUop
  // Probe on RFW
  // Probe on ALUsrcB
  // Probe on EXTop

  // Other names for the same wires on the sheet: bits27_20[7:0] = IW[27:20]
endmodule
