// Digital circuit instruction_memory.dig as structural Verilog
module instruction_memory (
  input  [6:0] A,
  input  [4:0] PN,
  output [31:0] D
);

  wire [31:0] _00_dp_reg_d, _01_dp_imm_d, _02_dp_lsl_imm_d, _03_dp_lsr_reg_d, _04_dp_asr_imm_d,
       _05_mem_reg_d, _06_mem_imm_d, _07_mem_shift_reg_d, _08_blbx_d, _09_b_d, _10_beq_d, _11_ble_d,
       _12_bgt_d, _13_mul_d, _14_rsb_d, _15_quadratic_d, _16_get_bitseq_d, _17_max3_d, _18_fib_rec_d,
       _19_sort_d, _20_merge_sort_d;

  ROM #(.AddrBits(7), .Bits(32)) _00_dp_reg (.A(A), .sel(1'b1), .D(_00_dp_reg_d));
  ROM #(.AddrBits(7), .Bits(32)) _01_dp_imm (.A(A), .sel(1'b1), .D(_01_dp_imm_d));
  ROM #(.AddrBits(7), .Bits(32)) _02_dp_lsl_imm (.A(A), .sel(1'b1), .D(_02_dp_lsl_imm_d));
  ROM #(.AddrBits(7), .Bits(32)) _03_dp_lsr_reg (.A(A), .sel(1'b1), .D(_03_dp_lsr_reg_d));
  ROM #(.AddrBits(7), .Bits(32)) _04_dp_asr_imm (.A(A), .sel(1'b1), .D(_04_dp_asr_imm_d));
  ROM #(.AddrBits(7), .Bits(32)) _05_mem_reg (.A(A), .sel(1'b1), .D(_05_mem_reg_d));
  ROM #(.AddrBits(7), .Bits(32)) _06_mem_imm (.A(A), .sel(1'b1), .D(_06_mem_imm_d));
  ROM #(.AddrBits(7), .Bits(32)) _07_mem_shift_reg (.A(A), .sel(1'b1), .D(_07_mem_shift_reg_d));
  ROM #(.AddrBits(7), .Bits(32)) _08_blbx (.A(A), .sel(1'b1), .D(_08_blbx_d));
  ROM #(.AddrBits(7), .Bits(32)) _09_b (.A(A), .sel(1'b1), .D(_09_b_d));
  ROM #(.AddrBits(7), .Bits(32)) _10_beq (.A(A), .sel(1'b1), .D(_10_beq_d));
  ROM #(.AddrBits(7), .Bits(32)) _11_ble (.A(A), .sel(1'b1), .D(_11_ble_d));
  ROM #(.AddrBits(7), .Bits(32)) _12_bgt (.A(A), .sel(1'b1), .D(_12_bgt_d));
  ROM #(.AddrBits(7), .Bits(32)) _13_mul (.A(A), .sel(1'b1), .D(_13_mul_d));
  ROM #(.AddrBits(7), .Bits(32)) _14_rsb (.A(A), .sel(1'b1), .D(_14_rsb_d));
  ROM #(.AddrBits(7), .Bits(32)) _15_quadratic (.A(A), .sel(1'b1), .D(_15_quadratic_d));
  ROM #(.AddrBits(7), .Bits(32)) _16_get_bitseq (.A(A), .sel(1'b1), .D(_16_get_bitseq_d));
  ROM #(.AddrBits(7), .Bits(32)) _17_max3 (.A(A), .sel(1'b1), .D(_17_max3_d));
  ROM #(.AddrBits(7), .Bits(32)) _18_fib_rec (.A(A), .sel(1'b1), .D(_18_fib_rec_d));
  ROM #(.AddrBits(7), .Bits(32)) _19_sort (.A(A), .sel(1'b1), .D(_19_sort_d));
  ROM #(.AddrBits(7), .Bits(32)) _20_merge_sort (.A(A), .sel(1'b1), .D(_20_merge_sort_d));
  Multiplexer #(.Selector_Bits(5), .Bits(32)) multiplexer_1 (
    .sel(PN), .in_0(_00_dp_reg_d), .in_1(_01_dp_imm_d), .in_2(_02_dp_lsl_imm_d), .in_3(_03_dp_lsr_reg_d),
    .in_4(_04_dp_asr_imm_d), .in_5(_05_mem_reg_d), .in_6(_06_mem_imm_d), .in_7(_07_mem_shift_reg_d),
    .in_8(_08_blbx_d), .in_9(_09_b_d), .in_10(_10_beq_d), .in_11(_11_ble_d), .in_12(_12_bgt_d),
    .in_13(_13_mul_d), .in_14(_14_rsb_d), .in_15(_15_quadratic_d), .in_16(_16_get_bitseq_d),
    .in_17(_17_max3_d), .in_18(_18_fib_rec_d), .in_19(_19_sort_d), .in_20(_20_merge_sort_d),
    .in_21({32{1'b0}}), .in_22({32{1'b0}}), .in_23({32{1'b0}}), .in_24({32{1'b0}}), .in_25({32{1'b0}}),
    .in_26({32{1'b0}}), .in_27({32{1'b0}}), .in_28({32{1'b0}}), .in_29({32{1'b0}}), .in_30({32{1'b0}}),
    .in_31({32{1'b0}}), .out(D));

  // Notes on the sheet:
  //   contents of _00_dp_reg (hex, n*v repeats v):
  //   e3a00000,e3a01001,e0800001,e2800000
  //   contents of _01_dp_imm (hex, n*v repeats v):
  //   e3a00002,e2400001,e2800000
  //   contents of _02_dp_lsl_imm (hex, n*v repeats v):
  //   e3a00001,e1a00100,e2800000
  //   contents of _03_dp_lsr_reg (hex, n*v repeats v):
  //   e3a00002,e3a01001,e1a00130,e2800000
  //   contents of _04_dp_asr_imm (hex, n*v repeats v):
  //   e3a00002,e1a000c0,e2800000
  //   contents of _05_mem_reg (hex, n*v repeats v):
  //   e3a0d0ff,e1a0d10d,e24dd008,e3a00001,e3a0c004,e58d0004,e3a00002
  //   ,e79d000c,e2800000
  //   contents of _06_mem_imm (hex, n*v repeats v):
  //   e3a0d0ff,e1a0d10d,e24dd008,e3a00001,e58d0004,e3a00002,e59d0004,e2800000
  //   contents of _07_mem_shift_reg (hex, n*v repeats v):
  //   e3a0d0ff,e1a0d10d,e24dd008,e3a00001,e3a0c001,e58d0004,e3a00002
  //   ,e79d010c,e2800000
  //   7
  //   contents of _08_blbx (hex, n*v repeats v):
  //   e3a00001,e3a01002,eb000000,e2800000,e0800001,e12fff1e
  //   contents of _09_b (hex, n*v repeats v):
  //   ea000003,e3a00000,e2400001,e2800001,e2800000,e3a00001,e2800000
  //   contents of _10_beq (hex, n*v repeats v):
  //   e3a01001,e3510001,a000001,e3a00000,e2800000,e3a00001,e2800000
  //   contents of _11_ble (hex, n*v repeats v):
  //   e3a01001,e3510002,da000001,e3a00000,e2800000,e3a00001,e2800000
  //   contents of _12_bgt (hex, n*v repeats v):
  //   e3a01001,e3510000,ca000001,e3a00000,e2800000,e3a00001,e2800000
  //   contents of _13_mul (hex, n*v repeats v):
  //   e3a01002,e3a02003,e0000291,e2800000
  //   contents of _14_rsb (hex, n*v repeats v):
  //   e3a00017,e2600046,e2800000
  //   14
  //   contents of _15_quadratic (hex, n*v repeats v):
  //   e3a00002,e3a01004,e3a02006,e3a03008,eb000000,e2800000,e0020290
  //   ,e0000090,e0000091,e0820000,e0830000,e12fff1e
  //   contents of _16_get_bitseq (hex, n*v repeats v):
  //   e3a0000d,e1a00280,e3a01005,e3a02007,eb000000,e2800000,e042c001
  //   ,e1a00130,e3a03001,e1a03f83,e1a03c53,e26cc01f,e1a03c33,e0000003,e12fff1e
  //   contents of _17_max3 (hex, n*v repeats v):
  //   e3a00001,e3a02003,e3a03002,eb000000,e2800000,e1500001,ca000000
  //   ,e1a00001,e1500002,ca000000,e1a00002,e12fff1e
  //   contents of _18_fib_rec (hex, n*v repeats v):
  //   e3a0d001,e1a0d50d,e3a0000a,eb000000,e2800000,e24dd008,e58de000
  //   ,e3500001,da000009,e2400001,e58d0004,ebfffff8,e1a01000,e59d0004
  //   ,e2400001,e58d1004,ebfffff3,e59d1004,e0800001,e59de000,e28dd008,e12fff1e
  //   contents of _19_sort (hex, n*v repeats v):
  //   e24dd030,e58d4000,e58d5004,e58d6008,e58d700c,e58d8010,e58d9014
  //   ,e58da018,e58db01c,e58dc020,e58dd024,e58de028,e1a04000,e1a05001
  //   ,e3a06000,e3a07000,e1560005,aa00000f,e0849007,e045a006,e1a00009
  //   ,e1a0100a,ebfffffe,e1a08100,e0888007,e794b008,e794c007,e15b000c
  //   ,da000001,e784b007,e784c008,e2866001,e2877004,eaffffed,e59de028
  //   ,e59dd024,e59dc020,e59db01c,e59da018,e59d9014,e59d8010,e59d700c
  //   ,e59d6008,e59d5004,e59d4000,e28dd030,e2800000
  //   contents of _20_merge_sort (hex, n*v repeats v):
  //   e24dd030,e3a04000,e3a05000,e3a06000,e58d0000,e58d1004,e58d2008
  //   ,e58d300c,e58d4010,e58d5014,e58d6018,e58d701c,e58d8020,e58d9024
  //   ,e58da028,e58dc02c,e0814002,e1a040a4,e1a05001,e2844001,e1a06004
  //   ,e2444001,e2411001,e1a0c001,e2811001,e28cc001,e15c0002,ca000031
  //   ,e1a09004,e2899001,e1550009,a00000d,e2822001,e1a0a002,e2422001
  //   ,e156000a,a000010,e1a05105,e7907005,e1a05125,e1a06106,e7908006
  //   ,e1a06126,e1570008,ba000010,ea000017,e1a06106,e7907006,e1a0c10c
  //   ,e783700c,e1a0c12c,e1a06126,e2866001,eaffffe2,e1a05105,e7907005
  //   ,e1a0c10c,e783700c,e1a0c12c,e1a05125,e2855001,eaffffda,e1a05105
  //   ,e7907005,e1a0c10c,e783700c,e1a0c12c,e1a05125,e2855001,eaffffd2
  //   ,e1a06106,e7907006,e1a0c10c,e783700c,e1a0c12c,e1a06126,e2866001
  //   ,eaffffca,e59dc02c,e59da028,e59d9024,e59d8020,e59d701c,e59d6018
  //   ,e59d5014,e59d4010,e59d300c,e59d2008,e59d1004,e59d0000,e1a0c001
  //   ,e3a07000,e15c0002,ca000005,e1a0c10c,e793700c,e780700c,e1a0c12c
  //   ,e28cc001,eafffff7,e28dd030,e12fff1e,e3a04000,e24dd018,e58de000
  //   ,e1520001,da000013,e0824001,e1a040a4,e58d2004,e58d4008,e1a02004
  //   ,ebfffff5,e59d4008,e59d2004,e58d1004,e58d4008,e1a01004,e2811001
  //   ,ebffffee,e59d4008,e59d1004,e58d1004,e58d2008,ebfffffe,e59d2008
  //   ,e59d1004,e59de000
  //   20
endmodule
