// Digital circuit project06.dig as structural Verilog
module project06 (
  input  CLK,
  input  CLR,
  input  [4:0] PROG,
  output [31:0] R0,
  output DONE,
  output [31:0] R2
);

  wire a_mul, ALUsrcB, C, CLK_t, i_dp, MR, MW, N, RFW, RR2sel, SHen, V, WDsel, Z;
  wire [1:0] EXTop, PCsel, RR0sel, RR1sel, WRsel;
  wire [2:0] ALUop;
  wire [3:0] cond, multiplexer_2_out, multiplexer_3_out, multiplexer_4_out, multiplexer_5_out, NZCV;
  wire [23:0] b_offset;
  wire [27:24] iw;
  wire [31:0] add_1_s, add_2_s, alu_1_r, dig_reg_cir_1_q, extender_unit_1_extimm, multiplexer_1_out,
       multiplexer_6_out, multiplexer_7_out, multiplexer_8_out, r1, r3, r4, r5, r6, r7, r8, r9, r10, r11,
       r12, r13, r14, r15, ramdualport_1_d, register_file_1_rd0, register_file_1_rd1, register_file_1_rd2,
       shifter_1_r;

  // Probe on {cond, iw[27:26], i_dp, iw[24], b_offset[23:22], a_mul, b_offset[20:0]}
  and and_1 (CLK_t, CLK, ~DONE);  // And
  control_unit control_unit_1 (
    .NCZV(NZCV), .CLK(CLK_t), .iw({cond, iw[27:26], i_dp, iw[24], b_offset[23:22], a_mul, b_offset[20:0]}),
    .SHen(SHen), .MW(MW), .MR(MR), .WDsel(WDsel), .WRsel(WRsel), .RR2sel(RR2sel), .RR1sel(RR1sel),
    .RR0sel(RR0sel), .PCsel(PCsel), .ALUop(ALUop), .ALUsrcB(ALUsrcB), .EXTop(EXTop), .RFW(RFW));
  dig_reg_cir dig_reg_cir_1 (.D(multiplexer_1_out), .CLK(CLK_t), .EN(1'b1), .CLR(CLR), .Q(dig_reg_cir_1_q));
  Multiplexer #(.Selector_Bits(2), .Bits(32)) multiplexer_1 (
    .sel(PCsel), .in_0(add_1_s), .in_1(multiplexer_8_out), .in_2(register_file_1_rd1), .in_3({32{1'b0}}),
    .out(multiplexer_1_out));
  instruction_memory instruction_memory_1 (
    .A(dig_reg_cir_1_q[8:2]), .PN(PROG),
    .D({cond, iw[27:26], i_dp, iw[24], b_offset[23:22], a_mul, b_offset[20:0]}));
  Add #(.Bits(32)) add_1 (.a(dig_reg_cir_1_q), .b(32'h4), .c_i(1'b0), .s(add_1_s));  // open: c_o
  // Probe on R0
  // Probe on r1
  // Probe on R2
  // Probe on r3
  // Probe on cond
  // Probe on cond
  // Probe on cond
  // Probe on cond
  // Probe on iw[27:26]
  // Probe on {iw[27:26], i_dp, iw[24], b_offset[23]}
  // Probe on iw[27:26]
  // Probe on {iw[27:26], i_dp}
  Add #(.Bits(32)) add_2 (.a(add_1_s), .b(32'h4), .c_i(1'b0), .s(add_2_s));  // open: c_o
  // Probe on r4
  // Probe on r5
  // Probe on r6
  // Probe on r7
  // Probe on i_dp
  // Probe on a_mul
  // Probe on i_dp
  // Probe on iw[24]
  // Probe on {iw[24], b_offset[23:22], a_mul}
  // Probe on b_offset[20]
  // Probe on iw[24]
  // Probe on {b_offset[23:22], a_mul, b_offset[20:0]}
  // Probe on r8
  // Probe on r9
  // Probe on r10
  // Probe on r11
  // Probe on b_offset[20]
  // Probe on b_offset[19:16]
  // Probe on b_offset[23]
  // Probe on b_offset[19:16]
  // Probe on b_offset[15:12]
  // Probe on b_offset[22]
  // Probe on r12
  // Probe on r13
  // Probe on r14
  // Probe on r15
  // Probe on b_offset[15:12]
  // Probe on a_mul
  // Probe on b_offset[3:0]
  // Probe on b_offset[11:8]
  // Probe on b_offset[20]
  // Probe on N
  // Probe on C
  // Probe on Z
  // Probe on V
  // Probe on b_offset[7:0]
  // Probe on b_offset[7:4]
  // Probe on b_offset[19:16]
  Multiplexer #(.Bits(4)) multiplexer_2 (.sel(RR2sel), .in_0(b_offset[11:8]), .in_1(4'b0000), .out(multiplexer_2_out));
  // Probe on b_offset[3:0]
  // Probe on b_offset[15:12]
  Multiplexer #(.Selector_Bits(2), .Bits(4)) multiplexer_3 (
    .sel(RR0sel), .in_0(b_offset[19:16]), .in_1(4'b1111), .in_2(b_offset[3:0]), .in_3(4'b0000),
    .out(multiplexer_3_out));
  Multiplexer #(.Selector_Bits(2), .Bits(4)) multiplexer_4 (
    .sel(RR1sel), .in_0(b_offset[3:0]), .in_1(b_offset[15:12]), .in_2(b_offset[11:8]), .in_3(4'b0000),
    .out(multiplexer_4_out));
  Multiplexer #(.Selector_Bits(2), .Bits(4)) multiplexer_5 (
    .sel(WRsel), .in_0(b_offset[15:12]), .in_1(4'b1110), .in_2(b_offset[19:16]), .in_3(4'b0000),
    .out(multiplexer_5_out));
  Multiplexer #(.Bits(32)) multiplexer_6 (
    .sel(WDsel), .in_0(multiplexer_8_out), .in_1(add_1_s), .out(multiplexer_6_out));
  // Probe on b_offset[3:0]
  register_file register_file_1 (
    .ReadReg0(multiplexer_3_out), .ReadReg1(multiplexer_4_out), .ReadReg2(multiplexer_2_out), .WriteEn(RFW),
    .WriteReg(multiplexer_5_out), .WriteData(multiplexer_6_out), .CLK(CLK_t), .CLR(CLR), .PC(add_2_s),
    .RD0(register_file_1_rd0), .RD1(register_file_1_rd1), .r0(R0), .r1(r1), .r2(R2), .r3(r3), .r4(r4),
    .r5(r5), .r6(r6), .r7(r7), .r8(r8), .r9(r9), .r10(r10), .r11(r11), .r12(r12), .r13(r13), .r14(r14),
    .r15(r15), .RD2(register_file_1_rd2));
  // Probe on b_offset[11:0]
  shifter shifter_1 (
    .iw({cond, iw[27:26], i_dp, iw[24], b_offset[23:22], a_mul, b_offset[20:0]}), .D(register_file_1_rd1),
    .Rs(register_file_1_rd2), .SHsel(SHen), .R(shifter_1_r));
  extender_unit extender_unit_1 (
    .iw({cond, iw[27:26], i_dp, iw[24], b_offset[23:22], a_mul, b_offset[20:0]}), .ExtOp(EXTop),
    .extimm(extender_unit_1_extimm));
  // Probe on extender_unit_1_extimm
  Multiplexer #(.Bits(32)) multiplexer_7 (
    .sel(ALUsrcB), .in_0(shifter_1_r), .in_1(extender_unit_1_extimm), .out(multiplexer_7_out));
  Comparator #(.Bits(32)) comparator_1 (
    .a({cond, iw[27:26], i_dp, iw[24], b_offset[23:22], a_mul, b_offset[20:0]}), .b(32'he2800000), .eq(DONE));  // open: gt, lt
  ALU alu_1 (
    .ALUOp(ALUop), .A(register_file_1_rd0), .B(multiplexer_7_out), .R(alu_1_r), .N(N), .Z(Z), .NZCV(NZCV),
    .C(C), .V(V));
  Multiplexer #(.Bits(32)) multiplexer_8 (.sel(MR), .in_0(alu_1_r), .in_1(ramdualport_1_d), .out(multiplexer_8_out));
  RAMDualPort #(.AddrBits(10), .Bits(32)) ramdualport_1 (
    .A(alu_1_r[9:0]), .Din(register_file_1_rd1), .str(MW), .C(CLK_t), .ld(MR), .D(ramdualport_1_d));

  // Other names for the same wires on the sheet: Imm[7:0] = b_offset[7:0]; immoff[11:0] = b_offset[11:0];
  //   iw (some bits) = {cond, i_dp, b_offset[23:22], a_mul, b_offset[20:0]}; rm[3:0] = b_offset[3:0];
  //   rm_mul[3:0] = b_offset[3:0]; opmul4[3:0] = b_offset[7:4]; rs_mul[3:0] = b_offset[11:8];
  //   rd[3:0] = b_offset[15:12]; rn_mul[3:0] = b_offset[15:12]; rd_mul[3:0] = b_offset[19:16];
  //   rn[3:0] = b_offset[19:16]; l_sdt = b_offset[20]; s_dp = b_offset[20]; s_mul = b_offset[20];
  //   b_offset[21] = a_mul; opc[3:0] = {iw[24], b_offset[23:22], a_mul}; w_sdt = a_mul; b_sdt = b_offset[22];
  //   opmul6[4:0] = {iw[27:26], i_dp, iw[24], b_offset[23]}; u_sdt = b_offset[23]; l_b = iw[24]; p_sdt = iw[24];
  //   i_sdt = i_dp; opb3[2:0] = {iw[27:26], i_dp}; op2[1:0] = iw[27:26]; opmul2[1:0] = iw[27:26]

  // Notes on the sheet:
  //   Tests
  //   00-dp-reg
  //   01-dp-imm
  //   02-dp-lsl-imm
  //   03-dp-lsr-reg
  //   04-dp-asr-imm
  //   05-mem-reg
  //   06-mem-imm
  //   07-mem-shift-reg
  //   08-blbx
  //   09-b
  //   10-beq
  //   11-ble
  //   12-bgt
  //   13-mul
  //   14-rsb
  //   15-quadratic
  //   16-getbit-seq
  //   17-max3
  //   18-fib-rec
endmodule
